// Logisim project cpu.circ as structural Verilog: 1 circuit, main circuit CPU
module CPU (
  input  [31:0] Instruction,
  input  CLK,
  output [31:0] s0,
  output [31:0] s1,
  output [31:0] t0,
  output [31:0] t1,
  output [31:0] a0,
  output [31:0] ra,
  output [31:0] sp,
  output [31:0] PC
);

  wire pc_1_p1;
  wire [31:0] bitselector_1_out, regfile_1_r1, regfile_1_r2;

  // PC pc_1: pin names not known; wires that end beside it: pc_1_p1, Instruction, Instruction
  Clock clock_1 (.out(CLK));
  // Incrementer incrementer_1: pin names not known; wires that end beside it: pc_1_p1, Instruction
  // memory_main main_1: pin names not known; wires that end beside it: CLK
  RegFile regfile_1 (
    .Clk(CLK), .R1(regfile_1_r1), .R2(regfile_1_r2), .W(Instruction), .RD(Instruction[4:0]),
    .RS1(Instruction[21:17]), .RS2(Instruction[31:27]), .s0(s0), .s1(s1), .t0(t0), .t1(t1), .a0(a0), .ra(ra),
    .sp(sp));  // open: WE
  BitSelector #(.width(32), .group(32)) bitselector_1 (.in(regfile_1_r2), .out(bitselector_1_out));  // open: sel
  ALU alu_1 (.A(regfile_1_r1), .B(bitselector_1_out));  // open: ALU_Op, Out
  // memory_main main_2: pin names not known

  assign PC = Instruction;

  // Other names for the same wires on the sheet: fetch_addr[31:0] = Instruction; INST[31:0] = Instruction

  // Notes on the sheet:
  //   NOTE
  //   Please do not modify/replace/move/change/delete/etc input and output pins
  //   These are debug/test outputs from your circuit
endmodule
