// Logisim project regfile.circ as structural Verilog: 1 circuit, main circuit RegFile
module RegFile (
  input  [4:0] RD,
  input  [4:0] RS1,
  input  [4:0] RS2,
  input  [31:0] W,
  input  WE,
  input  Clk,
  output [31:0] s0,
  output [31:0] s1,
  output [31:0] t0,
  output [31:0] t1,
  output [31:0] a0,
  output [31:0] ra,
  output [31:0] sp,
  output [31:0] R1,
  output [31:0] R2
);

  wire and_1_out, and_2_out, and_3_out, and_4_out, and_5_out, and_6_out, and_7_out, and_8_out, and_9_out,
       decoder_1_out0, decoder_1_out1, decoder_1_out2, decoder_1_out3, decoder_1_out4, decoder_1_out5,
       decoder_1_out6, decoder_1_out7, decoder_1_out8;
  wire [31:0] register_1_q, register_2_q, register_3_q, register_4_q, register_5_q, register_6_q,
       register_7_q, register_8_q, register_9_q;

  Decoder #(.select(5)) decoder_1 (
    .out0(decoder_1_out0), .out1(decoder_1_out1), .out2(decoder_1_out2), .out3(decoder_1_out3),
    .out4(decoder_1_out4), .out5(decoder_1_out5), .out6(decoder_1_out6), .out7(decoder_1_out7),
    .out8(decoder_1_out8), .sel(RD));  // open: out9, out10, out11, out12, out13, out14, out15, out16, out17, out18, out19, out20, out21, out22, out23, out24, out25, out26, out27, out28, out29, out30, out31, en
  and and_1 (and_1_out, decoder_1_out0, WE);
  and and_2 (and_2_out, decoder_1_out1, WE);
  and and_3 (and_3_out, decoder_1_out2, WE);
  and and_4 (and_4_out, decoder_1_out3, WE);
  and and_5 (and_5_out, decoder_1_out4, WE);
  and and_6 (and_6_out, decoder_1_out5, WE);
  and and_7 (and_7_out, decoder_1_out6, WE);
  and and_8 (and_8_out, decoder_1_out7, WE);
  and and_9 (and_9_out, decoder_1_out8, WE);
  Register #(.width(32)) register_1 (.Q(register_1_q), .clk(Clk), .clr(and_1_out));  // open: D, en
  Register #(.width(32)) register_2 (.D(W), .Q(register_2_q), .clk(Clk), .clr(and_2_out));  // open: en
  Register #(.width(32)) register_3 (.D(W), .Q(register_3_q), .clk(Clk), .clr(and_3_out));  // open: en
  Register #(.width(32)) register_4 (.D(W), .Q(register_4_q), .clk(Clk), .clr(and_4_out));  // open: en
  Register #(.width(32)) register_5 (.D(W), .Q(register_5_q), .clk(Clk), .clr(and_5_out));  // open: en
  Register #(.width(32)) register_6 (.D(W), .Q(register_6_q), .clk(Clk), .clr(and_6_out));  // open: en
  Register #(.width(32)) register_7 (.D(W), .Q(register_7_q), .clk(Clk), .clr(and_7_out));  // open: en
  Register #(.width(32)) register_8 (.D(W), .Q(register_8_q), .clk(Clk), .clr(and_8_out));  // open: en
  Register #(.width(32)) register_9 (.D(W), .Q(register_9_q), .clk(Clk), .clr(and_9_out));  // open: en
  Multiplexer #(.select(5), .width(32)) multiplexer_1 (
    .in0(register_1_q), .in1(register_2_q), .in2(register_3_q), .in3(register_4_q), .in4(register_5_q),
    .in5(register_6_q), .in6(register_7_q), .in7(register_8_q), .in8(register_9_q), .out(R1), .sel(RS1));  // open: in9, in10, in11, in12, in13, in14, in15, in16, in17, in18, in19, in20, in21, in22, in23, in24, in25, in26, in27, in28, in29, in30, in31, en
  Multiplexer #(.select(5), .width(32)) multiplexer_2 (
    .in0(register_1_q), .in1(register_2_q), .in2(register_3_q), .in3(register_4_q), .in4(register_5_q),
    .in5(register_6_q), .in6(register_7_q), .in7(register_8_q), .in8(register_9_q), .out(R2), .sel(RS2));  // open: in9, in10, in11, in12, in13, in14, in15, in16, in17, in18, in19, in20, in21, in22, in23, in24, in25, in26, in27, in28, in29, in30, in31, en

  // Notes on the sheet:
  //   Write Register
  //   Read Register 1
  //   Read Register 2
  //   Write Data
  //   Write Enable
  //   Clock
  //   NOTE
  //   Please do not modify/replace/move/change/delete/etc input and output pins
  //   These are debug/test outputs from your circuit
  //   Read Data 1
  //   Read Data 2
endmodule
